# Fritzing sketch plana automação v2.0 (saved by Fritzing 0.8.7b)
circuit board: 15cm x 15cm
breadboards: 1

parts:
  IC1 = L293D [package=THT]
  RL17 = Rele Generico [package=relay-g5q]
  RL18 = Rele Generico [package=relay-g5q]
  RL19 = Rele Generico [package=relay-g5q]
  RL21 = Rele Generico [package=relay-g5q]
  RL22 = Rele Generico [package=relay-g5q]
  RL23 = Rele Generico [package=relay-g5q]
  J27 = screw terminal, 3 pins
  J32 = screw terminal, 3 pins
  J33 = screw terminal, 3 pins
  J31 = screw terminal, 3 pins
  J30 = screw terminal, 3 pins
  J29 = screw terminal, 3 pins
  J28 = screw terminal, 3 pins
  RL20 = Rele Generico [package=relay-g5q]
  J34 = male alternating pin header, 2 pins [form="♂ (male)"]
  J35 = male pin header, 2 pins [form="♂ (male)"]
  J36 = male pin header, 2 pins [form="♂ (male)"]
  J37 = female pin header, 3 pins [form="♀ (female)"]
  XTAL7 = Crystal [frequency="16 Mhz" package=THT]
  C14 = Ceramic Capacitor [capacitance=100nF package="100 mil [THT, multilayer]"]
  C15 = Ceramic Capacitor [capacitance=100nF package="100 mil [THT, multilayer]"]
  S6 = Momentary Switch [package=ksa_sealed_tac_switch]
  Power_plug4 = Power plug
  U5 = Voltage Regulator - 5V [package="TO220 [THT]"]
  U4 = Voltage Regulator - 5V [package="TO220 [THT]"]
  R18 = Resistor [tolerance=±5% resistance=220 package=THT]
  C17 = Electrolytic Capacitor [capacitance=1000µF voltage=35V package="300 mil [THT, electrolytic]"]
  U6 = RELAY [package=relay-g5q]
  J43 = male pin header, 2 pins [form="♂ (male)"]
  D1 = Rectifier Diode [part_number=1N4001 package="300 mil [THT]"]
  U11 = Optocoupler [package=THT]
  Q9 = NPN-Transistor [package="TO92 [THT]"]
  U12 = Optocoupler [package=THT]
  Q10 = NPN-Transistor [package="TO92 [THT]"]
  R19 = Resistor [tolerance=±5% resistance=1k package=THT]
  R20 = Resistor [tolerance=±5% resistance=1k package=THT]
  J44 = male alternating pin header, 2 pins [form="♂ (male)"]
  J45 = male alternating pin header, 2 pins [form="♂ (male)"]
  R25 = Resistor [tolerance=±5% resistance=1k package=THT]
  R26 = Resistor [tolerance=±5% resistance=1k package=THT]
  J47 = male pin header, 2 pins [form="♂ (male)"]  # not connected
  U13 = Optocoupler [package=THT]
  R27 = Resistor [tolerance=±5% resistance=1k package=THT]
  Q11 = NPN-Transistor [package="TO92 [THT]"]
  J48 = male alternating pin header, 2 pins [form="♂ (male)"]
  R28 = Resistor [tolerance=±5% resistance=1k package=THT]
  J49 = female pin header, 3 pins [form="♀ (female)"]
  U3 = atmega328 [package=dip]
  U14 = Optocoupler [package=THT]
  Q12 = NPN-Transistor [package="TO92 [THT]"]
  R29 = Resistor [tolerance=±5% resistance=1k package=THT]
  J50 = male alternating pin header, 2 pins [form="♂ (male)"]
  R30 = Resistor [tolerance=±5% resistance=1k package=THT]

nets:
  N1: IC1.Enable_1, U3.A5
  N2: IC1.In_1, U3.A4
  N3: IC1.Out_1_(_Controlled_by_Enable_1_), U3.A3
  N4: IC1.0V, RL21.BOBINA2, RL20.BOBINA1, U3.A1, U3.A2
  N5: IC1.Out_2_(_Controlled_by_Enable_1_), U3.A0
  GND: IC1.+Vmotor, J36.pin1, J37.pin3, S6.3, S6.4, Power_plug4.GND, U5.GND, U4.GND, U11.Pin_5, U12.Pin_5, J44.pin2, J45.pin2, U13.Pin_5, J48.pin2, U3.GND#21, U14.Pin_5, J50.pin2
  N6: IC1.Enable_2, RL22.BOBINA2, RL23.BOBINA1, U5.input_voltage, U4.input_voltage, D1.cathode, U11.Pin_2, Q9.C, U12.Pin_2, Q10.C, J49.pin3, U14.Pin_2, Q12.C
  N7: IC1.In_3, RL23.BOBINA2
  N8: IC1.Out_3_(_Controlled_by_Enable_2_), RL22.BOBINA1
  N9: IC1.Out_4_(_Controlled_by_Enable_2_), RL19.BOBINA2
  N10: IC1.In_4, RL18.BOBINA1
  N11: RL17.ENTRADA, J27.pin2
  N12: RL17.NA, J27.pin1
  N13: RL17.BOBINA1, RL18.BOBINA2, RL19.BOBINA1, RL21.BOBINA1, RL20.BOBINA2
  N14: RL18.ENTRADA, J28.pin2
  N15: RL18.NA, J28.pin1
  N16: RL18.NF, J28.pin3
  N17: RL19.ENTRADA, J29.pin2
  N18: RL19.NA, J29.pin1
  N19: RL19.NF, J29.pin3
  N20: RL21.ENTRADA, J31.pin2
  N21: RL21.NA, J31.pin1
  N22: RL21.NF, J31.pin3
  N23: RL22.ENTRADA, J32.pin2
  N24: RL22.NA, J32.pin1
  N25: RL22.NF, J32.pin3
  N26: RL23.ENTRADA, J33.pin2
  N27: RL23.NA, J33.pin1
  N28: RL23.NF, J33.pin3
  N29: J30.pin1, RL20.NA
  N30: J30.pin2, RL20.ENTRADA
  N31: J30.pin3, RL20.NF
  N32: J34.pin1, U3.D12
  N33: J35.pin1, U3.D13
  N34: J37.pin1, U3.VCC, U3.AVCC
  N35: XTAL7.pin_0, C14.1, U3.XLAT1
  N36: XTAL7.pin_1, C15.1, U3.XLAT2
  N37: C14.0, C15.0, U3.GND#7
  N38: S6.1, R18.Pin_1
  N39: S6.2, U3.RESET
  N40: Power_plug4.VCC, D1.anode
  N41: U5.output_voltage, U4.output_voltage, J49.pin1
  N42: R18.Pin_0, C17.-
  N43: C17.+, U6.COIL1
  N44: J43.pin1, U3.D1_(TX)
  N45: J43.pin2, U3.D0_(RX)
  N46: U11.Pin_1, R20.Pin_1
  N47: U11.Pin_4, R25.Pin_0
  N48: Q9.E, J44.pin1
  N49: Q9.B, R20.Pin_0
  N50: U12.Pin_1, R19.Pin_1
  N51: U12.Pin_4, R26.Pin_0
  N52: Q10.E, J45.pin1
  N53: Q10.B, R19.Pin_0
  N54: U13.Pin_1, R27.Pin_1
  N55: U13.Pin_2, Q11.C, J49.pin2
  N56: U13.Pin_4, R28.Pin_0
  N57: R27.Pin_0, Q11.B
  N58: Q11.E, J48.pin1
  N59: U14.Pin_1, R29.Pin_0
  N60: U14.Pin_4, R30.Pin_0
  N61: Q12.E, J50.pin1
  N62: Q12.B, R29.Pin_1

custom parts:
  Rele Generico: MPA-S-105-C
